// Logisim project lock.circ as structural Verilog: 4 circuits, main circuit Lock
module Lock (
  input  Button_Input,
  output Message,
  output Lock_State
);

  wire Clock_out;

  Clock Clock (.out(Clock_out));
  Lock_Controller Lock_Controller (
    .Button_Input(Button_Input), .Clock(Clock_out), .Message(Message), .Lock_State(Lock_State));
endmodule

module Lock_Controller (
  input  Button_Input,
  input  Clock,
  output Message,
  output Lock_State
);

  wire _3_Bit_State_Register_out_5, _3_Bit_State_Register_out_6, _3_Bit_State_Register_out_7,
       Lock_Logic_out_7, Lock_Logic_out_8, Lock_Logic_out_9;

  Lock_Logic Lock_Logic (
    .in_1(Button_Input), .in_2(_3_Bit_State_Register_out_5), .in_3(_3_Bit_State_Register_out_6),
    .in_4(_3_Bit_State_Register_out_7), .out_5(Message), .out_6(Lock_State), .out_7(Lock_Logic_out_7),
    .out_8(Lock_Logic_out_8), .out_9(Lock_Logic_out_9));
  State_Register _3_Bit_State_Register (
    .in_1(Lock_Logic_out_7), .in_2(Lock_Logic_out_8), .in_3(Lock_Logic_out_9), .in_4(Clock),
    .out_5(_3_Bit_State_Register_out_5), .out_6(_3_Bit_State_Register_out_6),
    .out_7(_3_Bit_State_Register_out_7));
endmodule

module Lock_Logic (
  input  in_1,
  input  in_2,
  input  in_3,
  input  in_4,
  output out_5,
  output out_6,
  output out_7,
  output out_8,
  output out_9
);


  assign in_2 = in_1;
  assign in_3 = in_1;
  assign in_4 = in_1;
  assign out_5 = in_1;
  assign out_6 = in_1;
  assign out_7 = in_1;
  assign out_8 = in_1;
  assign out_9 = in_1;
endmodule

module State_Register (
  input  in_1,
  input  in_2,
  input  in_3,
  input  in_4,
  output out_5,
  output out_6,
  output out_7
);


  assign in_2 = in_1;
  assign in_3 = in_1;
  assign in_4 = in_1;
  assign out_5 = in_1;
  assign out_6 = in_1;
  assign out_7 = in_1;
endmodule
